// Logisim project Cache.circ as structural Verilog: 4 circuits, main circuit implementation
module implementation (
  input  [9:0] CpuAddressIn,
  input  CpuReadIn,
  input  CpuWriteIn,
  input  [7:0] CpuWriteValueIn,
  input  [31:0] LineFromMemIn,
  input  ClkIn,
  output ReadyOut,
  output DidContainOut,
  output [7:0] ByteReadOut,
  output [7:0] MemAddressOut,
  output MemReadOut,
  output MemWriteOut,
  output [31:0] Line2MemOut
);

  wire and_1_out, Contains, Dirty0, Dirty1, Init, Match0, Match1, multiplexer_4_out, or_1_out, Set0, Set1,
       t_ff_1_q;
  wire [1:0] multiplexer_5_out;
  wire [7:0] Byte0, Byte1, multiplexer_2_out;
  wire [9:0] Addr0, Addr1, multiplexer_3_out, WrtAddr;
  wire [31:0] Block0, Block1, multiplexer_6_out;

  Demultiplexer #(.enable("false")) demultiplexer_1 (.out0(Set0), .out1(Set1), .in(MemReadOut), .sel(CpuAddressIn[9]));
  Register #(.width(1)) register_1 (.D(Contains), .en(MemReadOut), .clk(ClkIn), .Q(DidContainOut));  // open: clr
  Multiplexer #(.enable("false")) multiplexer_1 (.in0(Match0), .in1(Match1), .out(Contains), .sel(CpuAddressIn[9]));
  Register register_2 (.D(multiplexer_2_out), .en(MemReadOut), .clk(ClkIn), .Q(ByteReadOut));  // open: clr
  Multiplexer #(.enable("false"), .width(8)) multiplexer_2 (
    .in0(Byte0), .in1(Byte1), .out(multiplexer_2_out), .sel(CpuAddressIn[9]));
  Multiplexer #(.enable("false"), .width(10)) multiplexer_3 (
    .in0(Addr0), .in1(Addr1), .out(multiplexer_3_out), .sel(CpuAddressIn[9]));
  Set set_1 (
    .ByteIn(CpuWriteValueIn), .BlockIn(LineFromMemIn), .Addr(CpuAddressIn), .Write(CpuWriteIn),
    .Initialize(Init), .Clock(ClkIn), .MatchSet(Set0), .ByteOut(Byte0), .BlockOut(Block0), .DirtyOut(Dirty0),
    .AddrOut(Addr0), .Match(Match0));
  Register #(.width(10)) register_3 (.D(multiplexer_3_out), .en(MemReadOut), .clk(ClkIn), .Q(WrtAddr));  // open: clr
  Multiplexer #(.enable("false")) multiplexer_4 (
    .in0(Dirty0), .in1(Dirty1), .out(multiplexer_4_out), .sel(CpuAddressIn[9]));
  or or_1 (or_1_out, ~MemReadOut, and_1_out);  // OR_Gate
  and and_1 (and_1_out, multiplexer_4_out, ~Contains);  // AND_Gate
  T_Flip_Flop Ready (.T(or_1_out), .clk(ClkIn), .Q(MemReadOut));  // open: Qn, reset, preset
  Multiplexer #(.enable("false"), .width(10)) multiplexer_5 (
    .in0(WrtAddr), .in1(CpuAddressIn), .out({MemAddressOut, multiplexer_5_out}), .sel(MemReadOut));
  Multiplexer #(.enable("false"), .width(32)) multiplexer_6 (
    .in0(Block0), .in1(Block1), .out(multiplexer_6_out), .sel(CpuAddressIn[9]));
  Register #(.width(32)) register_4 (
    .D(multiplexer_6_out), .en(MemReadOut), .clk(ClkIn), .Q(Line2MemOut));  // open: clr
  Set set_2 (
    .ByteIn(CpuWriteValueIn), .BlockIn(LineFromMemIn), .Addr(CpuAddressIn), .Write(CpuWriteIn),
    .Initialize(Init), .Clock(ClkIn), .MatchSet(Set1), .ByteOut(Byte1), .BlockOut(Block1), .DirtyOut(Dirty1),
    .AddrOut(Addr1), .Match(Match1));
  T_Flip_Flop t_ff_1 (.T(Init), .clk(ClkIn), .Q(t_ff_1_q));  // open: Qn, reset, preset
  nor nor_1 (MemWriteOut, MemReadOut, Init);
  not not_1 (Init, t_ff_1_q);

  assign ReadyOut = MemReadOut;

  // Other names for the same wires on the sheet: MemAddress[7:0] = MemAddressOut; clk = ClkIn;
  //   CpuAddress[9:0] = CpuAddressIn; SetBit = CpuAddressIn[9]; CpuRead = CpuReadIn; CpuWrite = CpuWriteIn;
  //   CpuWriteValue[7:0] = CpuWriteValueIn; DidContain = DidContainOut; LineFromMem[31:0] = LineFromMemIn;
  //   MemWrite = MemWriteOut; MemRead = MemReadOut; Ready = MemReadOut; ByteRead[7:0] = ByteReadOut;
  //   SelectedSetByteRead[7:0] = ByteReadOut; Line2Mem[31:0] = Line2MemOut; SelectedSetLine2Mem[31:0] = Line2MemOut
endmodule

module Set (
  input  [7:0] ByteIn,
  input  [31:0] BlockIn,
  input  [9:0] Addr,
  input  Write,
  input  Initialize,
  input  Clock,
  input  MatchSet,
  output [7:0] ByteOut,
  output [31:0] BlockOut,
  output DirtyOut,
  output [9:0] AddrOut,
  output Match
);

  wire and_1_out, and_2_out, and_3_out, and_5_out, and_6_out, Dirty0, Dirty1, Dirty2, Match0, Match1, Match2,
       or_1_out, or_3_out, or_4_out, Valid0, Valid1, Valid2;
  wire [7:0] Byte0, Byte1, Byte2, multiplexer_1_out, multiplexer_2_out, multiplexer_4_out;
  wire [9:0] multiplexer_3_out, multiplexer_7_out, Tag0, Tag1;
  wire [31:0] Blk0, Blk1, multiplexer_6_out, multiplexer_8_out;

  or or_1 (or_1_out, ~Match, Match1, Match2);  // OR_Gate
  and and_1 (and_1_out, or_1_out, MatchSet);
  or or_2 (Match, Match0, Match1, Match2);
  Multiplexer #(.enable("false"), .select(2), .width(8)) multiplexer_1 (
    .in0(BlockIn[7:0]), .in1(BlockIn[15:8]), .in2(BlockIn[23:16]), .in3(BlockIn[31:24]),
    .out(multiplexer_1_out), .sel(Addr[1:0]));
  Multiplexer #(.enable("false"), .width(8)) multiplexer_2 (
    .in0(multiplexer_1_out), .in1(Byte2), .out(multiplexer_2_out), .sel(Match2));
  Multiplexer #(.enable("false"), .width(10)) multiplexer_3 (
    .in0(Addr), .in1(AddrOut), .out(multiplexer_3_out), .sel(Match2));
  Way way_1 (
    .BlockIn(Blk0), .TagIn(Tag0), .DirtyIn(Dirty0), .ValidIn(Valid0), .Write(and_1_out),
    .Initialize(Initialize), .Clock(Clock), .ByteOut(Byte1), .BlockOut(Blk1), .TagOut(Tag1),
    .DirtyOut(Dirty1), .ValidOut(Valid1), .Match(Match1));
  Multiplexer #(.enable("false"), .width(8)) multiplexer_4 (
    .in0(multiplexer_2_out), .in1(Byte1), .out(multiplexer_4_out), .sel(Match1));
  and and_2 (and_2_out, Match2, Dirty2);
  or or_3 (or_3_out, and_2_out, and_3_out);
  and and_3 (and_3_out, Match1, Dirty1);
  Multiplexer #(.enable("false"), .width(8)) multiplexer_5 (
    .in0(multiplexer_4_out), .in1(Byte0), .out(ByteOut), .sel(Match0));
  Multiplexer #(.enable("false"), .width(32)) multiplexer_6 (
    .in0(BlockIn), .in1(BlockOut), .out(multiplexer_6_out), .sel(Match2));
  Multiplexer #(.enable("false"), .width(10)) multiplexer_7 (
    .in0(multiplexer_3_out), .in1(Tag1), .out(multiplexer_7_out), .sel(Match1));
  Multiplexer #(.enable("false"), .width(32)) multiplexer_8 (
    .in0(multiplexer_6_out), .in1(Blk1), .out(multiplexer_8_out), .sel(Match1));
  and and_4 (DirtyOut, Dirty2, Valid2, ~Match);  // AND_Gate
  and and_5 (and_5_out, Write, MatchSet);
  or or_4 (or_4_out, ~Match, Match2);  // OR_Gate
  and and_6 (and_6_out, or_4_out, MatchSet);
  Way0 way0_1 (
    .ByteIn(ByteIn), .BlockIn(multiplexer_8_out), .TagIn(multiplexer_7_out), .DirtyIn(or_3_out),
    .WriteByte(and_5_out), .MatchSet(MatchSet), .Initialize(Initialize), .Clock(Clock), .ByteOut(Byte0),
    .BlockOut(Blk0), .TagOut(Tag0), .DirtyOut(Dirty0), .ValidOut(Valid0), .Match(Match0));
  Way way_2 (
    .BlockIn(Blk1), .TagIn(Tag1), .DirtyIn(Dirty1), .ValidIn(Valid1), .Write(and_6_out),
    .Initialize(Initialize), .Clock(Clock), .ByteOut(Byte2), .BlockOut(BlockOut), .TagOut(AddrOut),
    .DirtyOut(Dirty2), .ValidOut(Valid2), .Match(Match2));

  // Other names for the same wires on the sheet: Blk2[31:0] = BlockOut; Clk = Clock; Init = Initialize;
  //   Tag2[9:0] = AddrOut
endmodule

module Way (
  input  [31:0] BlockIn,
  input  [9:0] TagIn,
  input  DirtyIn,
  input  ValidIn,
  input  Write,
  input  Initialize,
  input  Clock,
  output [7:0] ByteOut,
  output [31:0] BlockOut,
  output [9:0] TagOut,
  output DirtyOut,
  output ValidOut,
  output Match
);

  wire and_1_out, and_2_out, and_3_out, and_4_out, or_1_out, or_2_out;
  wire [7:0] xnor_1_out;

  and and_1 (and_1_out, DirtyIn, Write);
  and and_2 (and_2_out, ValidIn, Write);
  or or_1 (or_1_out, DirtyOut, and_1_out);
  and and_3 (and_3_out, or_1_out, ~Initialize);  // AND_Gate
  or or_2 (or_2_out, ValidOut, and_2_out);
  Register #(.width(32)) Data (.D(BlockIn), .en(Write), .clk(Clock), .Q(BlockOut));  // open: clr
  Register Tag (.D(TagIn[9:2]), .en(Write), .clk(Clock), .Q(TagOut[9:2]));  // open: clr
  D_Flip_Flop Dirty (.D(and_3_out), .clk(Clock), .Q(DirtyOut));  // open: Qn, preset, reset
  D_Flip_Flop Valid (.D(and_4_out), .clk(Clock), .Q(ValidOut));  // open: Qn, preset, reset
  and and_4 (and_4_out, or_2_out, ~Initialize);  // AND_Gate
  assign xnor_1_out = ~(TagIn[9:2] ^ TagOut[9:2]);  // XNOR_Gate xnor_1, 8 bits wide
  Multiplexer #(.enable("false"), .select(2), .width(8)) multiplexer_1 (
    .in0(BlockOut[7:0]), .in1(BlockOut[15:8]), .in2(BlockOut[23:16]), .in3(BlockOut[31:24]), .out(ByteOut),
    .sel(TagIn[1:0]));
  and and_5 (Match, xnor_1_out[0], xnor_1_out[1], xnor_1_out[2], xnor_1_out[3], xnor_1_out[4], xnor_1_out[5], xnor_1_out[6], xnor_1_out[7], ValidOut);

  assign TagOut[1:0] = 2'b00;

  // Other names for the same wires on the sheet: Clk = Clock; Init = Initialize; Blk[1:0] = TagIn[1:0];
  //   Tag[7:0] = TagIn[9:2]; TagOut_t[7:0] = TagOut[9:2]
endmodule

module Way0 (
  input  [7:0] ByteIn,
  input  [31:0] BlockIn,
  input  [9:0] TagIn,
  input  DirtyIn,
  input  WriteByte,
  input  MatchSet,
  input  Initialize,
  input  Clock,
  output [7:0] ByteOut,
  output [31:0] BlockOut,
  output [9:0] TagOut,
  output DirtyOut,
  output ValidOut,
  output Match
);

  wire and_2_out, and_3_out, and_4_out, D0Wrt, D1Wrt, D2Wrt, D3Wrt, or_1_out, or_2_out, or_3_out, or_4_out,
       or_5_out, or_6_out, WriteBlk;
  wire [7:0] multiplexer_1_out, multiplexer_2_out, multiplexer_3_out, multiplexer_4_out, xnor_1_out;

  Demultiplexer #(.enable("false"), .select(2)) demultiplexer_1 (
    .out0(D0Wrt), .out1(D1Wrt), .out2(D2Wrt), .out3(D3Wrt), .in(WriteByte), .sel(TagIn[1:0]));
  and and_1 (WriteBlk, MatchSet, ~Match);  // AND_Gate
  and and_2 (and_2_out, WriteBlk, DirtyIn);
  Multiplexer #(.enable("false"), .width(8)) multiplexer_1 (
    .in0(BlockIn[7:0]), .in1(ByteIn), .out(multiplexer_1_out), .sel(D0Wrt));
  or or_1 (or_1_out, WriteBlk, D0Wrt);
  Multiplexer #(.enable("false"), .width(8)) multiplexer_2 (
    .in0(BlockIn[23:16]), .in1(ByteIn), .out(multiplexer_2_out), .sel(D2Wrt));
  or or_2 (or_2_out, WriteBlk, D2Wrt);
  or or_3 (or_3_out, DirtyOut, WriteByte, and_2_out);
  or or_4 (or_4_out, ValidOut, WriteBlk);
  and and_3 (and_3_out, or_4_out, ~Initialize);  // AND_Gate
  Register Data0 (.D(multiplexer_1_out), .en(or_1_out), .clk(Clock), .Q(BlockOut[7:0]));  // open: clr
  Register Data2 (.D(multiplexer_2_out), .en(or_2_out), .clk(Clock), .Q(BlockOut[23:16]));  // open: clr
  Register Tag (.D(TagIn[9:2]), .en(WriteBlk), .clk(Clock), .Q(TagOut[9:2]));  // open: clr
  D_Flip_Flop Dirty (.D(and_4_out), .clk(Clock), .Q(DirtyOut));  // open: Qn, preset, reset
  and and_4 (and_4_out, or_3_out, ~Initialize);  // AND_Gate
  D_Flip_Flop Valid (.D(and_3_out), .clk(Clock), .Q(ValidOut));  // open: Qn, preset, reset
  Multiplexer #(.enable("false"), .width(8)) multiplexer_3 (
    .in0(BlockIn[15:8]), .in1(ByteIn), .out(multiplexer_3_out), .sel(D1Wrt));
  or or_5 (or_5_out, WriteBlk, D1Wrt);
  Multiplexer #(.enable("false"), .width(8)) multiplexer_4 (
    .in0(BlockIn[31:24]), .in1(ByteIn), .out(multiplexer_4_out), .sel(D3Wrt));
  or or_6 (or_6_out, WriteBlk, D3Wrt);
  Register Data1 (.D(multiplexer_3_out), .en(or_5_out), .clk(Clock), .Q(BlockOut[15:8]));  // open: clr
  Register Data3 (.D(multiplexer_4_out), .en(or_6_out), .clk(Clock), .Q(BlockOut[31:24]));  // open: clr
  assign xnor_1_out = ~(TagIn[9:2] ^ TagOut[9:2]);  // XNOR_Gate xnor_1, 8 bits wide
  and and_5 (Match, xnor_1_out[0], xnor_1_out[1], xnor_1_out[2], xnor_1_out[3], xnor_1_out[4], xnor_1_out[5], xnor_1_out[6], xnor_1_out[7], ValidOut);
  Multiplexer #(.enable("false"), .select(2), .width(8)) multiplexer_5 (
    .in0(BlockOut[7:0]), .in1(BlockOut[15:8]), .in2(BlockOut[23:16]), .in3(BlockOut[31:24]), .out(ByteOut),
    .sel(TagIn[1:0]));

  assign TagOut[1:0] = 2'b00;

  // Other names for the same wires on the sheet: BIn[7:0] = ByteIn; D0In[7:0] = BlockIn[7:0];
  //   D1In[7:0] = BlockIn[15:8]; D2In[7:0] = BlockIn[23:16]; D3In[7:0] = BlockIn[31:24]; D0Out[7:0] = BlockOut[7:0];
  //   D1Out[7:0] = BlockOut[15:8]; D2Out[7:0] = BlockOut[23:16]; D3Out[7:0] = BlockOut[31:24]; Clk = Clock;
  //   Init = Initialize; Blk[1:0] = TagIn[1:0]; Tag[7:0] = TagIn[9:2]; TagOut_t[7:0] = TagOut[9:2];
  //   WrtByte = WriteByte
endmodule
