// Logisim project adder4.circ as structural Verilog: 1 circuit, main circuit implementation
module implementation (
  input  [3:0] Ain,
  input  [3:0] Bin,
  input  Cinin,
  output [3:0] Sum_Out,
  output Carry_Out
);

  wire and_1_out, and_2_out, and_3_out, and_4_out, and_6_out, and_7_out, and_8_out, and_9_out, and_10_out,
       and_11_out, C0, C1, C2, G0, G1, G2, G3, P0, P1, P2, P3;

  and and_1 (and_1_out, P3, G2);
  and and_2 (and_2_out, P2, P3, G1);
  and and_3 (and_3_out, P1, G0, P3, P2);
  and and_4 (and_4_out, P1, P0, P3, P2, Cinin);
  or or_1 (Carry_Out, G3, and_1_out, and_2_out, and_3_out, and_4_out);
  assign {G3, G2, G1, G0} = Ain & Bin;  // AND_Gate and_5, 4 bits wide
  assign {P3, P2, P1, P0} = Ain ^ Bin;  // XOR_Gate xor_1, 4 bits wide
  and and_6 (and_6_out, P0, Cinin);
  and and_7 (and_7_out, P1, G0);
  and and_8 (and_8_out, P1, Cinin, P0);
  and and_9 (and_9_out, P2, G1);
  and and_10 (and_10_out, P2, P1, G0);
  and and_11 (and_11_out, P1, Cinin, P0, P2);
  or or_2 (C0, G0, and_6_out);
  or or_3 (C1, G1, and_7_out, and_8_out);
  or or_4 (C2, G2, and_9_out, and_10_out, and_11_out);
  assign Sum_Out = {C2, C1, C0, Cinin} ^ Ain ^ Bin;  // XOR_Gate xor_2, 4 bits wide

  // Other names for the same wires on the sheet: Cin = Cinin; A[3:0] = Ain; B[3:0] = Bin; C3 = Carry_Out;
  //   Sum[3:0] = Sum_Out
endmodule
