// Logisim project multiplier.circ as structural Verilog: 1 circuit, main circuit main
module main (
  input  [3:0] in_1,
  input  [3:0] in_2,
  input  in_3,
  output [7:0] out_4,
  output ready
);

  wire bitselector_1_out, clock_1_out, clock_2_out, clock_3_out, or_1_out, StartMult;
  wire [1:0] index;
  wire [3:0] A, adder_1_out, B, multiplexer_1_out;
  wire [4:4] adder_1_cout;
  wire [7:0] multiplexer_2_out;

  Multiplexer #(.enable("false"), .select(2), .width(4)) multiplexer_1 (
    .in0(out_4[3:0]), .in1(out_4[4:1]), .in2(out_4[5:2]), .in3(out_4[6:3]), .out(multiplexer_1_out),
    .sel(index));
  Register #(.width(4)) register_1 (.D(in_1), .en(StartMult), .clk(clock_1_out), .Q(A));  // open: clr
  Clock clock_1 (.out(clock_1_out));
  Register #(.width(4)) register_2 (.D(in_2), .en(StartMult), .clk(clock_2_out), .Q(B));  // open: clr
  Clock clock_2 (.out(clock_2_out));
  Adder #(.width(4)) adder_1 (.a(A), .b(multiplexer_1_out), .out(adder_1_out), .cout(adder_1_cout[4]));  // open: cin
  BitSelector #(.width(4)) bitselector_1 (.in(B), .out(bitselector_1_out), .sel(index));
  Multiplexer #(.enable("false"), .width(8)) multiplexer_2 (
    .in1({8{1'b0}}), .out(multiplexer_2_out), .sel(StartMult));  // open: in0
  or or_1 (or_1_out, StartMult, bitselector_1_out);
  Clock clock_3 (.out(clock_3_out));
  Register register_3 (.D(multiplexer_2_out), .en(or_1_out), .clk(clock_3_out), .Q(out_4));  // open: clr

  // Other names for the same wires on the sheet: T2 = out_4[1]; total[7:0] = out_4; T1 = out_4[0]; T3 = out_4[2];
  //   T4 = out_4[3]; T5 = out_4[4]; T6 = out_4[5]; T7 = out_4[6]; Ain[3:0] = in_1; Bin[3:0] = in_2; Start = in_3;
  //   T8 = out_4[7]
endmodule
