// Logisim project shifter.circ as structural Verilog: 1 circuit, main circuit implementation
module implementation (
  input  IsRightShiftIn,
  input  IsArithmeticIn,
  input  [1:0] ShiftAmountIn,
  input  [2:0] NumberIn,
  output [2:0] ShiftedNumberOut
);

  wire multiplexer_1_out, multiplexer_2_out, multiplexer_3_out, multiplexer_5_out, multiplexer_6_out,
       multiplexer_7_out, multiplexer_8_out, multiplexer_9_out, multiplexer_10_out, or_1_out, or_2_out;

  Multiplexer #(.enable("false")) multiplexer_1 (
    .in0(1'b0), .in1(NumberIn[2]), .out(multiplexer_1_out), .sel(IsArithmeticIn));
  Multiplexer #(.enable("false"), .select(2)) multiplexer_2 (
    .in0(NumberIn[1]), .in1(NumberIn[0]), .in2(1'b0), .in3(1'b0), .out(multiplexer_2_out), .sel(ShiftAmountIn));
  Multiplexer #(.enable("false"), .select(2)) multiplexer_3 (
    .in0(NumberIn[1]), .in1(NumberIn[2]), .in2(multiplexer_1_out), .in3(multiplexer_1_out),
    .out(multiplexer_3_out), .sel(ShiftAmountIn));
  Multiplexer #(.enable("false")) multiplexer_4 (
    .in0(multiplexer_2_out), .in1(multiplexer_3_out), .out(ShiftedNumberOut[1]), .sel(IsRightShiftIn));
  Multiplexer #(.enable("false")) multiplexer_5 (
    .in0(1'b0), .in1(NumberIn[2]), .out(multiplexer_5_out), .sel(IsArithmeticIn));
  or or_1 (or_1_out, ShiftAmountIn[1], ShiftAmountIn[0]);
  Multiplexer #(.enable("false")) multiplexer_6 (
    .in0(1'b0), .in1(NumberIn[2]), .out(multiplexer_6_out), .sel(IsArithmeticIn));
  Multiplexer #(.enable("false")) multiplexer_7 (
    .in0(NumberIn[0]), .in1(1'b0), .out(multiplexer_7_out), .sel(or_1_out));
  Multiplexer #(.enable("false"), .select(2)) multiplexer_8 (
    .in0(NumberIn[0]), .in1(NumberIn[1]), .in2(NumberIn[2]), .in3(multiplexer_5_out),
    .out(multiplexer_8_out), .sel(ShiftAmountIn));
  Multiplexer #(.enable("false"), .select(2)) multiplexer_9 (
    .in0(NumberIn[2]), .in1(NumberIn[1]), .in2(NumberIn[0]), .in3(1'b0), .out(multiplexer_9_out),
    .sel(ShiftAmountIn));
  Multiplexer #(.enable("false")) multiplexer_10 (
    .in0(NumberIn[2]), .in1(multiplexer_6_out), .out(multiplexer_10_out), .sel(or_2_out));
  or or_2 (or_2_out, ShiftAmountIn[1], ShiftAmountIn[0]);
  Multiplexer #(.enable("false")) multiplexer_11 (
    .in0(multiplexer_7_out), .in1(multiplexer_8_out), .out(ShiftedNumberOut[0]), .sel(IsRightShiftIn));
  Multiplexer #(.enable("false")) multiplexer_12 (
    .in0(multiplexer_9_out), .in1(multiplexer_10_out), .out(ShiftedNumberOut[2]), .sel(IsRightShiftIn));

  // Other names for the same wires on the sheet: IsArithmetic = IsArithmeticIn; IsRightShift = IsRightShiftIn;
  //   N1 = NumberIn[0]; Number[2:0] = NumberIn; N2 = NumberIn[1]; N3 = NumberIn[2]; ShiftAmount[1:0] = ShiftAmountIn;
  //   S1 = ShiftedNumberOut[0]; ShiftedNumber[2:0] = ShiftedNumberOut; S2 = ShiftedNumberOut[1];
  //   S3 = ShiftedNumberOut[2]
endmodule
